// Logisim project ALU.circ as structural Verilog: 2 circuits, main circuit ALU_4
module ALU_4 (
  input  [3:0] a,
  input  [3:0] b,
  input  [2:0] sel,
  output [3:0] out_4,
  output Carry_out
);

  wire alu_1_out_6, alu_2_out_6, alu_3_out_6, and_1_out, not_1_out, not_2_out;

  ALU alu_1 (.S(out_4[0]), .sel(sel), .a(a[0]), .b(b[0]), .Carry_in(and_1_out), .out_6(alu_1_out_6));
  ALU alu_2 (.S(out_4[1]), .sel(sel), .a(a[1]), .b(b[1]), .Carry_in(alu_1_out_6), .out_6(alu_2_out_6));
  ALU alu_3 (.S(out_4[2]), .sel(sel), .a(a[2]), .b(b[2]), .Carry_in(alu_2_out_6), .out_6(alu_3_out_6));
  ALU alu_4 (.S(out_4[3]), .sel(sel), .a(a[3]), .b(b[3]), .Carry_in(alu_3_out_6), .out_6(Carry_out));
  and and_1 (and_1_out, sel[2], not_1_out, not_2_out);
  not not_1 (not_1_out, sel[1]);
  not not_2 (not_2_out, sel[0]);
endmodule

module ALU (
  input  Carry_in,
  input  a,
  input  b,
  input  [2:0] sel,
  output S,
  output out_6
);

  wire and_1_out, and_2_out, fulladder_1_carry_out, fulladder_1_s, fulladder_2_carry_out, fulladder_2_s,
       not_1_out, not_2_out, not_3_out, not_4_out, or_1_out;

  FullAdder fulladder_1 (.Carry_in(Carry_in), .a(a), .b(b), .S(fulladder_1_s), .Carry_out(fulladder_1_carry_out));
  not not_1 (not_1_out, b);
  or or_1 (or_1_out, a, b);
  and and_1 (and_1_out, a, b);
  not not_2 (not_2_out, b);
  FullAdder fulladder_2 (
    .Carry_in(Carry_in), .a(a), .b(not_1_out), .S(fulladder_2_s), .Carry_out(fulladder_2_carry_out));
  Mux_2_1 mux_2_1_1 (.a(fulladder_1_carry_out), .b(fulladder_2_carry_out), .S(out_6), .sel(and_2_out));
  not not_3 (not_3_out, sel[0]);
  and and_2 (and_2_out, not_3_out, not_4_out, sel[2]);
  not not_4 (not_4_out, sel[1]);
  Mux_8_1 mux_8_1_1 (
    .in_1(fulladder_1_s), .in_2(or_1_out), .in_3(and_1_out), .in_4(not_2_out), .in_5(fulladder_2_s),
    .in_9(sel), .out_10(S));  // open: in_6, in_7, in_8
endmodule
