// Logisim project RegFile.circ as structural Verilog: 3 circuits, main circuit main
module main (
  input  [3:0] dIn,
  input  [3:0] XSel,
  input  [3:0] YSel,
  input  [3:0] wSel,
  output [3:0] dbgA,
  output [3:0] dbgB,
  output [3:0] dbgC,
  output [3:0] dbgD,
  output [3:0] XOut,
  output [3:0] YOut
);

  Reg_4 reg_4_1 (.in_1(dIn), .in_3(wSel[0]), .out_4(dbgA));  // open: in_2
  Reg_4 reg_4_2 (.in_1(dIn), .in_3(wSel[1]), .out_4(dbgB));  // open: in_2
  Reg_4 reg_4_3 (.in_1(dIn), .in_3(wSel[2]), .out_4(dbgC));  // open: in_2
  Reg_4 reg_4_4 (.in_1(dIn), .in_3(wSel[3]), .out_4(dbgD));  // open: in_2
  Sel sel_1 (.A(dbgA), .B(dbgB), .C(dbgC), .D(dbgD), .Out(XOut), .Sel(XSel));
  Sel sel_2 (.A(dbgA), .B(dbgB), .C(dbgC), .D(dbgD), .Out(YOut), .Sel(YSel));
endmodule

module Sel (
  input  [3:0] A,
  input  [3:0] B,
  input  [3:0] C,
  input  [3:0] D,
  input  [3:0] Sel,
  output [3:0] Out
);

  wire nor_1_out;
  wire [3:0] controlled_buffer_1_out;

  assign controlled_buffer_1_out = Sel[0] ? A : 4'bz;  // Controlled_Buffer controlled_buffer_1
  assign controlled_buffer_1_out = Sel[1] ? B : 4'bz;  // Controlled_Buffer controlled_buffer_2
  assign controlled_buffer_1_out = Sel[2] ? C : 4'bz;  // Controlled_Buffer controlled_buffer_3
  assign controlled_buffer_1_out = Sel[3] ? D : 4'bz;  // Controlled_Buffer controlled_buffer_4
  assign controlled_buffer_1_out = nor_1_out ? 4'b0000 : 4'bz;  // Controlled_Buffer controlled_buffer_5
  nor nor_1 (nor_1_out, Sel[0], Sel[1], Sel[2], Sel[3]);
  assign Out = controlled_buffer_1_out;  // Buffer buffer_1, 4 bits wide
endmodule

module dSel (
  input  [3:0] ALUIn,
  input  [3:0] RAMIn,
  input  Sel,
  output [3:0] Out
);

  Multiplexer #(.width(4), .enable("false")) multiplexer_1 (.in0(ALUIn), .in1(RAMIn), .out(Out), .sel(Sel));
endmodule
