// Logisim project UC.circ as structural Verilog: 12 circuits, main circuit UC
// wREG
module UC (
  input  [11:0] RI_In,
  input  RESET,
  input  [3:0] PCIn,
  output [11:0] RI_Out,
  output [3:0] out_5,
  output read,
  output [3:0] rX,
  output [3:0] rY,
  output [3:0] mAD,
  output write,
  output [2:0] function_sel,
  output [3:0] PCOut,
  output wPC
);

  wire isjump_1_out_2, not_1_out, readregisterx_1_out_2, readregistery_1_out_2, writeregister_1_out_2;
  wire [1:0] readxsel_1_out;
  wire [3:0] pcsel_1_pcout;

  isJump isjump_1 (.in_1(RI_In[11:8]), .out_2(isjump_1_out_2));
  not not_1 (not_1_out, isjump_1_out_2);
  PCSel pcsel_1 (.in_1(PCIn), .PCOut(pcsel_1_pcout), .reset(RESET));
  assign PCOut = not_1_out ? pcsel_1_pcout : 4'bz;  // Controlled_Buffer controlled_buffer_1
  assign PCOut = isjump_1_out_2 ? RI_In[7:4] : 4'bz;  // Controlled_Buffer controlled_buffer_2
  Clock clock_1 (.out(wPC));
  isStore isstore_1 (.in_1(RI_In[11:8]), .out_2(write));
  writeRegister writeregister_1 (.CodOP(RI_In[11:8]), .out_2(writeregister_1_out_2));
  readXsel readxsel_1 (.X(RI_In[5:4]), .RES(RI_In[7:6]), .Out(readxsel_1_out), .Sel(RI_In[11:8]));
  readRegisterX readregisterx_1 (.CodOP(RI_In[11:8]), .out_2(readregisterx_1_out_2));
  registerSelector registerselector_1 (
    .A(rY[0]), .B(rY[1]), .C(rY[2]), .D(rY[3]), .sel(RI_In[3:2]), .activate(readregistery_1_out_2));
  readRegisterY readregistery_1 (.in_1(RI_In[11:8]), .out_2(readregistery_1_out_2));
  registerSelector registerselector_2 (
    .A(out_5[0]), .B(out_5[1]), .C(out_5[2]), .D(out_5[3]), .sel(RI_In[7:6]), .activate(writeregister_1_out_2));
  isLoad isload_1 (.in_1(RI_In[11:8]), .out_2(read));
  registerSelector registerselector_3 (
    .A(rX[0]), .B(rX[1]), .C(rX[2]), .D(rX[3]), .sel(readxsel_1_out), .activate(readregisterx_1_out_2));
  function_sel function_sel_1 (.in_1(RI_In[11:8]), .out_2(function_sel));

  assign mAD = {RI_In[5:4], RI_In[7:6]};
  assign RI_Out = RI_In;
endmodule

module function_sel (
  input  [3:0] in_1,
  output [2:0] out_2
);

  wire not_1_out;

  and and_1 (out_2[0], in_1[0], not_1_out);
  not not_1 (not_1_out, in_1[2]);

  assign out_2[2:1] = in_1[2:1];
endmodule

module registerSelector (
  input  [1:0] sel,
  input  activate,
  output A,
  output B,
  output C,
  output D
);

  wire and_1_out, and_2_out, and_3_out, and_4_out, not_1_out, not_2_out, not_3_out, not_4_out;

  not not_1 (not_1_out, sel[0]);
  not not_2 (not_2_out, sel[1]);
  not not_3 (not_3_out, sel[1]);
  not not_4 (not_4_out, sel[0]);
  Mux_2_1 mux_2_1_1 (.a(1'b0), .b(and_1_out), .S(A), .sel(activate));
  and and_1 (and_1_out, not_1_out, not_2_out);
  Mux_2_1 mux_2_1_2 (.a(1'b0), .b(and_2_out), .S(B), .sel(activate));
  and and_2 (and_2_out, sel[0], not_3_out);
  Mux_2_1 mux_2_1_3 (.a(1'b0), .b(and_3_out), .S(C), .sel(activate));
  and and_3 (and_3_out, not_4_out, sel[1]);
  Mux_2_1 mux_2_1_4 (.a(1'b0), .b(and_4_out), .S(D), .sel(activate));
  and and_4 (and_4_out, sel[0], sel[1]);
endmodule

module PCSel (
  input  [3:0] in_1,
  input  reset,
  output [3:0] PCOut
);

  wire not_1_out;
  wire [3:0] halfadder_1_result;

  HalfAdder halfadder_1 (.Result(halfadder_1_result[0]), .a(in_1[0]), .b(1'b1));  // open: Carry_out
  FullAdder fulladder_1 (.a(in_1[1]), .b(1'b0), .S(halfadder_1_result[1]));  // open: Carry_out
  FullAdder fulladder_2 (.a(in_1[2]), .b(1'b0), .S(halfadder_1_result[2]));  // open: Carry_out
  FullAdder fulladder_3 (.a(in_1[3]), .b(1'b0), .S(halfadder_1_result[3]));  // open: Carry_out
  Multiplexer #(.width(4), .disabled(0), .enable("false")) multiplexer_1 (
    .in0(4'b0000), .in1(halfadder_1_result), .out(PCOut), .sel(not_1_out));
  not not_1 (not_1_out, reset);
endmodule

module writeRegister (
  input  [3:0] CodOP,
  output out_2
);

  not not_1 (out_2, CodOP[3]);
endmodule

module readRegisterX (
  input  [3:0] CodOP,
  output out_2
);

  not not_1 (out_2, CodOP[2]);
endmodule

module readRegisterY (
  input  [3:0] in_1,
  output out_2
);

  wire not_1_out, not_2_out;

  not not_1 (not_1_out, in_1[2]);
  not not_2 (not_2_out, in_1[3]);
  and and_1 (out_2, not_1_out, not_2_out);
endmodule

module isStore (
  input  [3:0] in_1,
  output out_2
);

  wire not_1_out, not_2_out, not_3_out;

  not not_1 (not_1_out, in_1[1]);
  not not_2 (not_2_out, in_1[0]);
  and and_1 (out_2, not_2_out, not_1_out, not_3_out, in_1[3]);
  not not_3 (not_3_out, in_1[2]);
endmodule

module isLoad (
  input  [3:0] in_1,
  output out_2
);

  wire not_1_out, not_3_out;

  not not_1 (not_1_out, in_1[0]);
  // NOT_Gate not_2 has open pins: in=in_1[1], out=open
  not not_3 (not_3_out, in_1[3]);
  and and_1 (out_2, not_1_out, in_1[2], not_3_out);
endmodule

module readXsel (
  input  [1:0] X,
  input  [1:0] RES,
  input  [3:0] Sel,
  output [1:0] Out
);

  wire and_1_out, not_1_out, not_2_out, not_3_out;

  and and_1 (and_1_out, Sel[3], not_1_out, not_2_out, not_3_out);
  not not_1 (not_1_out, Sel[2]);
  Multiplexer #(.width(2), .enable("false")) multiplexer_1 (.in0(X), .in1(RES), .out(Out), .sel(and_1_out));
  not not_2 (not_2_out, Sel[1]);
  not not_3 (not_3_out, Sel[0]);
endmodule

module proto (
  input  [3:0] in_1,
  input  [3:0] in_2,
  input  [3:0] in_3,
  input  in_4,
  output [3:0] out_5,
  output [3:0] out_6
);

  wire isjump_1_out_2, not_1_out;
  wire [3:0] pcsel_1_pcout;

  assign out_5 = isjump_1_out_2 ? in_1 : 4'bz;  // Controlled_Buffer controlled_buffer_1
  isJump isjump_1 (.in_1(in_2), .out_2(isjump_1_out_2));
  not not_1 (not_1_out, isjump_1_out_2);
  PCSel pcsel_1 (.in_1(in_3), .PCOut(pcsel_1_pcout), .reset(in_4));
  assign out_5 = not_1_out ? pcsel_1_pcout : 4'bz;  // Controlled_Buffer controlled_buffer_2
endmodule

module isJump (
  input  [3:0] in_1,
  output out_2
);

  wire not_1_out, not_2_out;

  not not_1 (not_1_out, in_1[1]);
  not not_2 (not_2_out, in_1[2]);
  and and_1 (out_2, in_1[0], not_2_out, in_1[3]);
endmodule
